# Fritzing sketch BOM_washdrypcv_kill (saved by Fritzing 1.0.4)
circuit board: 9.92813cm x 9.57264cm
breadboards: 1

parts:
  J528 = screw terminal, 2 pins
  J529 = screw terminal, 2 pins
  J530 = female pin header, 1 pin [form="♀ (female)"]
  R43 = Resistor [tolerance=±5% resistance=220 power=0.25W package=THT]
  J531 = female pin header, 3 pins [form="♀ (female)"]  # not connected
  Q28 = NPN-Transistor [package="TO92 [THT]"]
  J532 = female pin header, 2 pins [form="♀ (female)"]
  J533 = female pin header, 1 pin [form="♀ (female)"]
  J534 = female pin header, 1 pin [form="♀ (female)"]
  J535 = female pin header, 1 pin [form="♀ (female)"]
  J536 = female pin header, 1 pin [form="♀ (female)"]
  J537 = female pin header, 2 pins [form="♀ (female)"]
  J538 = female pin header, 3 pins [form="♀ (female)"]
  R44 = Resistor [tolerance=±5% resistance=220 power=0.25W package=THT]
  Q29 = NPN-Transistor [package="TO92 [THT]"]
  Q30 = NPN-Transistor [package="TO92 [THT]"]
  Q31 = NPN-Transistor [package="TO92 [THT]"]
  Q32 = NPN-Transistor [package="TO92 [THT]"]
  Q33 = NPN-Transistor [package="TO92 [THT]"]
  R45 = Resistor [tolerance=±5% resistance=220 power=0.25W package=THT]
  R46 = Resistor [tolerance=±5% resistance=220 power=0.25W package=THT]
  R47 = Resistor [tolerance=±5% resistance=220 power=0.25W package=THT]
  R48 = Resistor [tolerance=±5% resistance=220 power=0.25W package=THT]
  R49 = Resistor [tolerance=±5% resistance=220 power=0.25W package=THT]
  J539 = female pin header, 4 pins [form="♀ (female)"]
  J540 = female pin header, 17 pins [form="♀ (female)"]
  J541 = female pin header, 17 pins [form="♀ (female)"]
  Part13 = Arduino Micro (Rev3)
  J542 = female pin header, 4 pins [form="♀ (female)"]
  J543 = female pin header, 4 pins [form="♀ (female)"]
  J544 = female pin header, 3 pins [form="♀ (female)"]
  J545 = female pin header, 4 pins [form="♀ (female)"]
  J546 = female pin header, 4 pins [form="♀ (female)"]
  J547 = female pin header, 2 pins [form="♀ (female)"]
  J548 = female pin header, 1 pin [form="♀ (female)"]
  J549 = female pin header, 1 pin [form="♀ (female)"]
  J550 = female pin header, 1 pin [form="♀ (female)"]
  J551 = female pin header, 1 pin [form="♀ (female)"]
  J552 = female pin header, 1 pin [form="♀ (female)"]
  J553 = female pin header, 1 pin [form="♀ (female)"]
  J554 = female pin header, 1 pin [form="♀ (female)"]
  J555 = female pin header, 1 pin [form="♀ (female)"]
  J556 = female pin header, 2 pins [form="♀ (female)"]
  J557 = female pin header, 1 pin [form="♀ (female)"]
  J558 = female pin header, 2 pins [form="♀ (female)"]
  J559 = female pin header, 3 pins [form="♀ (female)"]
  J560 = female pin header, 3 pins [form="♀ (female)"]
  J561 = female pin header, 1 pin [form="♀ (female)"]
  J562 = female pin header, 1 pin [form="♀ (female)"]
  J563 = female pin header, 1 pin [form="♀ (female)"]
  J564 = female pin header, 1 pin [form="♀ (female)"]
  J565 = female pin header, 1 pin [form="♀ (female)"]
  J566 = female pin header, 1 pin [form="♀ (female)"]
  J567 = female pin header, 1 pin [form="♀ (female)"]
  J568 = female pin header, 3 pins [form="♀ (female)"]
  J569 = female pin header, 1 pin [form="♀ (female)"]
  J570 = female pin header, 1 pin [form="♀ (female)"]
  J571 = female pin header, 1 pin [form="♀ (female)"]
  J572 = female pin header, 1 pin [form="♀ (female)"]
  J573 = female pin header, 1 pin [form="♀ (female)"]
  J574 = female pin header, 1 pin [form="♀ (female)"]
  J575 = female pin header, 3 pins [form="♀ (female)"]
  J576 = female pin header, 1 pin [form="♀ (female)"]
  J577 = female pin header, 1 pin [form="♀ (female)"]
  J578 = female pin header, 1 pin [form="♀ (female)"]
  J579 = female pin header, 1 pin [form="♀ (female)"]
  J580 = female pin header, 1 pin [form="♀ (female)"]
  J581 = female pin header, 3 pins [form="♀ (female)"]
  J582 = female pin header, 1 pin [form="♀ (female)"]
  J583 = female pin header, 1 pin [form="♀ (female)"]
  J584 = female pin header, 1 pin [form="♀ (female)"]
  J585 = female pin header, 17 pins [form="♀ (female)"]
  J586 = female pin header, 17 pins [form="♀ (female)"]

nets:
  N1: J528.pin1, Q33.C, J547.pin1, J580.pin1, J582.pin1, J584.pin1
  N2: J528.pin2, J544.pin2, J547.pin2, J557.pin1, J558.pin1
  N3: J529.pin1, J530.pin1, Q30.C, Q31.C, Q32.C, J545.pin1, J545.pin2, J545.pin3, J545.pin4, J555.pin1, J561.pin1, J562.pin1, J567.pin1, J569.pin1, J570.pin1, J573.pin1, J574.pin1, J578.pin1
  N4: J529.pin2, J546.pin1, J546.pin2, J546.pin3, J546.pin4
  N5: R43.Pin_0, Q28.E
  N6: R43.Pin_1, J532.pin2
  N7: Q28.B, J534.pin1, J535.pin1
  N8: Q28.C, J532.pin1, J533.pin1, J536.pin1
  N9: J537.pin1, J538.pin3, R44.Pin_1
  N10: J537.pin2, J538.pin2
  N11: J538.pin1, R44.Pin_0
  N12: Q29.B, J565.pin1
  N13: Q30.E, J563.pin1
  N14: Q30.B, J566.pin1
  N15: Q31.E, J571.pin1
  N16: Q31.B, J572.pin1
  N17: Q32.E, J577.pin1
  N18: Q32.B, J576.pin1
  N19: Q33.E, J583.pin1
  N20: Q33.B, J544.pin1, J579.pin1
  N21: R45.Pin_0, J559.pin3
  N22: R45.Pin_1, Part13.D13_PWM, J585.pin1
  N23: R46.Pin_0, J560.pin3
  N24: R47.Pin_0, J568.pin3
  N25: R48.Pin_0, J575.pin3
  N26: R49.Pin_0, J581.pin3
  N27: J539.pin1, J539.pin2, J539.pin3, J539.pin4, Part13.GND, J585.pin14, J586.pin12
  N28: J540.pin11, Part13.D6_PWM/A7, J553.pin1, J586.pin7
  N29: J541.pin7, J585.pin11
  N30: J541.pin8, J585.pin10
  N31: Part13.MOSI, J586.pin17
  N32: Part13.RXLED/SS, J586.pin16
  N33: Part13.D1/TX, J586.pin15
  N34: Part13.D0/RX, J586.pin14
  N35: Part13.RESET, J585.pin13, J586.pin13
  N36: Part13.D2/SDA, J586.pin11
  N37: Part13.D3/SCL, J586.pin10
  N38: Part13.D4_PWM/A6, J586.pin9
  N39: Part13.D5_PWM, J554.pin1, J586.pin8
  N40: Part13.D7, J586.pin6
  N41: Part13.D8_PWM/A8, J586.pin5
  N42: Part13.D9_PWM/A9, J552.pin1, J586.pin4
  N43: Part13.D10_PWM/A10, J548.pin1, J586.pin3
  N44: Part13.D11_PWM, J544.pin3, J586.pin2
  N45: Part13.D12_PWM/A11, J586.pin1
  N46: Part13.SCK, J585.pin17
  N47: Part13.MISO, J585.pin16
  N48: Part13.VIN, J585.pin15
  N49: Part13.5V, J585.pin12
  N50: Part13.A5, J585.pin9
  N51: Part13.A4, J585.pin8
  N52: Part13.A3, J585.pin7
  N53: Part13.A2, J585.pin6
  N54: Part13.A1, J585.pin5
  N55: Part13.A0, J556.pin2, J585.pin4
  N56: Part13.AREF, J585.pin3
  N57: Part13.3V3, J585.pin2
  N58: J542.pin1, J543.pin1
  N59: J542.pin2, J543.pin2, J549.pin1, J560.pin2
  N60: J542.pin3, J543.pin3, J550.pin1, J568.pin2
  N61: J542.pin4, J543.pin4, J551.pin1, J575.pin2
  N62: J556.pin1, J559.pin1, J564.pin1

notes:
  + -
  5V
  12V
  electrocaloric
  A0 -
  - +
  servo
  - 5v D11
